// Logisim project Simulation.circ as structural Verilog
// fA
module fulladder (
  input  a,
  input  b,
  input  cin,
  output sum,
  output cout
);

  wire half_adder_1_cout, half_adder_1_s, half_adder_2_cout;

  Half_Adder half_adder_1 (.a(a), .b(b), .s(half_adder_1_s), .cout(half_adder_1_cout));
  Half_Adder half_adder_2 (.a(half_adder_1_s), .b(cin), .s(sum), .cout(half_adder_2_cout));
  or or_1 (cout, half_adder_2_cout, half_adder_1_cout);
endmodule

// INC
module ALU (
  input  [2:0] a,
  input  [2:0] b,
  input  [2:0] Selector,
  input  cin,
  input  cin_2,
  output [2:0] Result,
  output Zero_Flag
);

  wire not_1_out, not_2_out, not_3_out;
  wire [2:0] _2_S_CMP_sum, ADD_out_3, AND_output, CMP_out_2, INC_out_2, OR_out_3, SUB_out, XOR_out_3;

  SUB SUB (.A(a), .B(b), .in_1(cin), .out(SUB_out));
  _2_S_CMP _2_S_CMP (.cin(cin_2), .a(a), .sum(_2_S_CMP_sum));
  AND AND (.a(a), .b(b), .\output (AND_output));
  OR_GATE OR (.a(a), .b(b), .out_3(OR_out_3));
  XORGATE XOR (.a(a), .b(b), .out_3(XOR_out_3));
  CMP_GATE CMP (.b(b), .out_2(CMP_out_2));
  ADD ADD (.B(b), .A(a), .out_3(ADD_out_3));
  INC INC (.A(a), .out_2(INC_out_2));
  Multiplexer #(.select(3), .width(3)) multiplexer_1 (
    .in0(AND_output), .in1(OR_out_3), .in2(XOR_out_3), .in3(CMP_out_2), .in4(ADD_out_3), .in5(SUB_out),
    .in6(_2_S_CMP_sum), .in7(INC_out_2), .out(Result), .sel(Selector));  // open: en
  not not_1 (not_1_out, Result[0]);
  not not_2 (not_2_out, Result[1]);
  not not_3 (not_3_out, Result[2]);
  and and_2 (Zero_Flag, not_1_out, not_2_out, not_3_out);
endmodule

module Half_Adder (
  input  a,
  input  b,
  output s,
  output cout
);

  xor xor_1 (s, a, b);
  and and_1 (cout, a, b);
endmodule

module _3_bit_fulladder (
  input  [2:0] A,
  input  cin,
  input  [2:0] B,
  output Overflow,
  output [2:0] Sum,
  output cout
);

  wire fulladder_1_cout, fulladder_2_cout;

  xor xor_1 (Overflow, fulladder_2_cout, cout);
  fulladder fulladder_1 (.a(A[0]), .b(B[0]), .cin(cin), .sum(Sum[0]), .cout(fulladder_1_cout));
  fulladder fulladder_2 (.a(A[1]), .b(B[1]), .cin(fulladder_1_cout), .sum(Sum[1]), .cout(fulladder_2_cout));
  fulladder fulladder_3 (.a(A[2]), .b(B[2]), .cin(fulladder_2_cout), .sum(Sum[2]), .cout(cout));
endmodule

module OR_GATE (
  input  [2:0] a,
  input  [2:0] b,
  output [2:0] out_3
);

  assign out_3 = a | b;  // OR_Gate or_1, 3 bits wide
endmodule

module XORGATE (
  input  [2:0] a,
  input  [2:0] b,
  output [2:0] out_3
);

  assign out_3 = a ^ b;  // XOR_Gate xor_1, 3 bits wide
endmodule

module CMP_GATE (
  input  [2:0] b,
  output [2:0] out_2
);

  assign out_2 = ~b;  // NOT_Gate not_1, 3 bits wide
endmodule

module ADD (
  input  [2:0] B,
  input  [2:0] A,
  output [2:0] out_3
);

  _3_bit_fulladder u_3_bit_fulladder_1 (.A(A), .B(B), .cin(1'b0), .Sum(out_3));  // open: Overflow, cout
endmodule

module SUB (
  input  in_1,
  input  [2:0] A,
  input  [2:0] B,
  output [2:0] out
);

  wire [2:0] not_1_out;

  assign not_1_out = ~B;  // NOT_Gate not_1, 3 bits wide
  _3_bit_fulladder u_3_bit_fulladder_1 (.A(A), .B(not_1_out), .cin(in_1), .Sum(out));  // open: Overflow, cout
endmodule

module _2_S_CMP (
  input  cin,
  input  [2:0] a,
  output [2:0] sum
);

  wire [2:0] not_1_out;

  assign not_1_out = ~a;  // NOT_Gate not_1, 3 bits wide
  _3_bit_fulladder u_3_bit_fulladder_1 (.A(not_1_out), .B(3'b000), .cin(cin), .Sum(sum));  // open: Overflow, cout
endmodule

module AND (
  input  [2:0] a,
  input  [2:0] b,
  output [2:0] \output 
);

  assign \output  = a & b;  // AND_Gate and_1, 3 bits wide
endmodule

module INC (
  input  [2:0] A,
  output [2:0] out_2
);

  _3_bit_fulladder u_3_bit_fulladder_1 (.A(A), .B(3'b000), .cin(1'b1), .Sum(out_2));  // open: Overflow, cout
endmodule
